# Fritzing sketch Circuit diagram (saved by Fritzing 0.9.0b)
breadboards: 1

parts:
  Raspberry_Pi_B_rev1 = Raspberry Pi B rev1
  S1 = SWITCH-MOMENTARY-2 [package=tactile-pth]
  LED1 = smd LED [color="Red (633nm)" package="0805 [SMD]"]
  R1 = Resistor [tolerance=±5% resistance=220 package="0805 [SMD]"]
  R2 = Resistor [package="2512 [SMD]"]
  LED2 = smd LED [color="Red (633nm)" package="0805 [SMD]"]

nets:
  N1: Raspberry_Pi_B_rev1.GND, S1.2, R1.Pin_1, R2.Pin_1
  N2: Raspberry_Pi_B_rev1.GPIO_18, S1.1
  N3: Raspberry_Pi_B_rev1.GPIO_24, LED1.anode
  N4: Raspberry_Pi_B_rev1.GPIO_25, LED2.anode
  N5: LED1.cathode, R1.Pin_0
  N6: R2.Pin_0, LED2.cathode

notes:
  Need to connect
  - wifi dongle
  - USB Microphone (to allow PCM recording)
  - speaker (either via HDMI or Audio Jack)
